# Fritzing sketch pi-pico-rtc (saved by Fritzing 0.9.6b)
breadboards: 1

parts:
  A1 = Raspberry Pi Pico H
  S1 = Momentary Switch [package=tactile-pth]
  Part2 = Adafruit DS3231 [part_number="Adafruit #3013"]

nets:
  GND: A1.GND, S1.2, Part2.GND
  N1: A1.GP4, Part2.SDA
  N2: A1.GP5, Part2.SCL
  N3: A1.RUN, S1.3
  N4: A1.3V3OUT, Part2.Vin

custom parts:
  Raspberry Pi Pico H: Raspberry Pi Pico H. Based around the RP2040 microcontroller the Pico H is a low cost microcontroller device bringing Raspberry Pi quality, cost, and easy of use to the microcontroller space.
  Adafruit DS3231: The datasheet for the DS3231 explains that this part is an "Extremely Accurate I²C-Integrated RTC/TCXO/Crystal". And, hey, it does exactly what it says on the tin! This Real Time Clock (RTC) is the most precise you can get in a small, low power package. Most RTCs use an external 32kHz timing crystal that is used to keep time with low current draw. And that's all well and good, but those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
